# Fritzing sketch Wiring Diagram (saved by Fritzing 0.9.3b)
breadboards: 1

parts:
  Teensy_3_2 = Teensy 3.1
  DRV8833 = Adafruit DRV8833 DC/Stepper Motor Driver [part_number="Adafruit #3297"]
  MOTOR1 = 28BYJ-48 Stepper Motor
  S1 = Pushbutton [package="[THT]"]

nets:
  N1: Teensy_3_2.D3, DRV8833.AIN1
  N2: Teensy_3_2.D4, DRV8833.AIN2
  N3: Teensy_3_2.D5, DRV8833.BIN2
  N4: Teensy_3_2.D6, DRV8833.BIN1
  N5: Teensy_3_2.3V3, DRV8833.!SLEEP
  N6: DRV8833.GND, MOTOR1.RED, S1.Pin_1, S1.Pin_2
  N7: DRV8833.AOUT2, MOTOR1.PINK
  N8: DRV8833.AOUT1, MOTOR1.ORANGE
  N9: DRV8833.BOUT1, MOTOR1.BLUE
  N10: DRV8833.BOUT2, MOTOR1.YELLOW

notes:
  5VDC
  Power
  Supply
  Stepper Motor
  Home
  Switch

custom parts:
  Adafruit DRV8833 DC/Stepper Motor Driver: Spin two DC motors or step one bi-polar or uni-polar stepper with up to 1.2A per channel using the DRV8833. This motor driver chip is a nice alternative to the TB6612 driver. Like that chip, you get 2 full H-bridges, but this chip is better for low voltage uses (can run from 2.7V up to 10.8V motor power) and has built in current limiting capability. We set it up for 1A current limiting so you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
